# Fritzing sketch Domotech (saved by Fritzing 0.9.6b)
breadboards: 2

parts:
  HC-05 = Bluetooth HC-05 Macho
  DHT11 = Humidity and Temperature Sensor DHT11
  Speaker = SPEAKER [package=pcb_mount_speaker]
  R9 = Resistor [tolerance=±5% resistance=220 power=0.25 package=THT]
  R10 = Resistor [tolerance=±5% resistance=220 power=0.25 package=THT]
  R11 = Resistor [tolerance=±5% resistance=220 power=0.25 package=THT]
  R12 = Resistor [tolerance=±5% resistance=220 power=0.25 package=THT]
  LED_Sala = LED - 5mm [color="White (8000K)" current=0.030 package="5 mm [THT]"]
  LED_Comedor = LED - 5mm [color="White (8000K)" current=0.030 package="5 mm [THT]"]
  LED_Cocina = LED - 5mm [color="White (8000K)" current=0.030 package="5 mm [THT]"]
  LED_Garaje = LED - 5mm [color="White (8000K)" current=0.030 package="5 mm [THT]"]
  Led_Verde_Alarma = LED - 3mm [color="Green (570nm)" current=0.030 package="3 mm [THT]"]
  Led_Rojo_Alarma = LED - 3mm [color="Red (660nm)" current=0.030 package="3 mm [THT]"]
  R15 = Resistor [tolerance=±5% resistance=220 power=0.25 package=THT]
  R16 = Resistor [tolerance=±5% resistance=220 power=0.25 package=THT]
  Part1 = Arduino Uno (Rev3)
  Part2 = HC-SR501 Body Sensor Module

nets:
  N1: HC-05.TXD, Part1.D10_PWM/SS
  N2: HC-05.RXD, Part1.D11_PWM/MOSI
  VCC: DHT11.Vcc, Part2.VCC
  N3: DHT11.Data-signal, Part1.D9_PWM
  GND: DHT11.GND_2, LED_Sala.cathode, LED_Comedor.cathode, LED_Cocina.cathode, LED_Garaje.cathode, R15.Pin_1, R16.Pin_1, Part1.GND, Part2.GND
  N4: Speaker.-, Part1.D13/SCK
  N5: R9.Pin_0, R9.Pin_1, LED_Sala.anode
  N6: R10.Pin_0, R10.Pin_1, LED_Comedor.anode
  N7: R11.Pin_0, R11.Pin_1, LED_Cocina.anode
  N8: R12.Pin_0, R12.Pin_1, LED_Garaje.anode
  N9: Led_Verde_Alarma.cathode, R15.Pin_0
  N10: Led_Verde_Alarma.anode, Part1.D7
  N11: Led_Rojo_Alarma.cathode, R16.Pin_0
  N12: Led_Rojo_Alarma.anode, Part1.D8
  N13: Part1.D12/MISO, Part2.OUT

notes:
  Buzzer
  HC-05, hay que configurarlo correctamente para su funcionamiento
  Sensor de Temperatura y Humedad DHT11
  Led's Interiores
  Sensor PIR para detectar movimiento dentro de la casa

custom parts:
  Humidity and Temperature Sensor DHT11: Digital relative humidity & temperature sensor DHT11
  HC-SR501 Body Sensor Module: Pyroelectric Infrared PIR Motion Sensor Detector Module

// code stored in the sketch: Casa_Domotica_Version_Final_y_Optimizada.ino
// LÍBRERIAS
#include <SoftwareSerial.h> //Libreria Software Serial para Bluetooth
#include <DHT.h> //Librería paa usar sensores DHT
#include <DHT_U.h> //Complemento de la librería DHT

//PINES ESPECIALES
#define DHTPIN 6 //Se define el pin del DHT
#define DHTTYPE DHT11 //Se define el tipo de sensor DHT-11

//OBJETOS DE LAS LIBRERÍAS
DHT dht(DHTPIN, DHTTYPE); // Crea un objeto de la librería DHT, indicando así el sensor
SoftwareSerial BT(10,11); //Definir los pines RX y TX del Arduino conectados al Bluetooth

//OBJETOS
char Mensaje; //Variable que mandara los mensajes a los Switches y por voz

// Bocina
const int buzzer = 13; //Bocina conectada al Pin 13

//Sistema de IR
const int sensorPin = 12; //Sensor de IR conectado al Pin 12 
const int LEDIV = 31; //Led Interior Verde
const int LEDIR = 30; //Led Interior Rojo
int luz = 0; //Valor para leer el dato de la luz       


//Sistema de luces interiores
const int LEDR1 = 36; //Led Habitacion Grande 1
const int LEDR2 = 37; //Led Habitacion Grande 2
const int LEDR3 = 38; //Led Habitacion Pequeña 1
const int LEDP1 = 39; //Led Habitacion Pequeña 2

//Variables para almacenar las lecturas del sensor DHT11
float celsius;
float fahrenheit;
float humedad;

void setup() {
  Serial.begin(9600); 
  BT.begin(38400); //Inicializamos el puerto serie BT (Para Modo AT 2)
  dht.begin(); //Comunicacion con el DHT11
  Serial.println("Iniciando todos los sistemas... Listo"); //Mensaje para indicar que esta listo
  
  //Se establecen los pines como entradas o salidas
  //Todos los LED's se establecen como Salida
  pinMode(sensorPin, INPUT); //Se establece como Entrada
  pinMode(buzzer, OUTPUT);
  pinMode(LEDIV,OUTPUT);
  pinMode(LEDIR,OUTPUT);
  

  pinMode(LEDR1, OUTPUT); 
  pinMode(LEDR2, OUTPUT);
  pinMode(LEDR3, OUTPUT); 
  pinMode(LEDP1, OUTPUT);

}                      
  }
  
  //SISTEMA DE TEMPERATURA Y HUMEDAD
  celsius = dht.readTemperature();  //Lee y almacena la temperatura del sensor DHT11
  fahrenheit = dht.readTemperature(true);  //Lee y almacena la temperatura del sensor DHT11
  humedad = dht.readHumidity();         //Lee y almacena la humedad del sensor DHT11
  valor_sensor = analogRead(A0);  //Lee el valor del sensor LDR
  valor_luz = map(valor_sensor, 1024, 0, 0, 255);  //Mapeo de los valores de la fotocelda en un rango de 0 a 255 %
  
  //Envía los datos del DHT11 como la temperatura, humedad e intensidad a la aplicación móvil por medio del Bluetooth
  BT.print(celsius);    
  BT.print(" °C");
  BT.print("|");
  BT.print(fahrenheit);
  BT.print(" °F");
  BT.print("|");
  BT.print(humedad);
  BT.print(" %");
  BT.print("|");
  BT.print(valor_luz);
  BT.print(" %");
  delay(1000);

  //Se envían los datos del DHT11 al Monitor Serie
  Serial.print(celsius);
  Serial.print(" °C");
  Serial.print("|");
  Serial.print(fahrenheit);
  Serial.print(" °F");
  Serial.print("|");
  Serial.print(humedad);
  Serial.print(" %");
  Serial.print("|");
  Serial.print(valor_luz);
  Serial.print(" %");
  delay(1000);

//SISTEMA DE ALARMA AL ENTRAR EN LA PUERTA
  int value = 0; //Declaramos una variable llamada value donde guardara el valor de la luz leida por el sensor
  value = digitalRead(sensorPin); //el valor va a ser leido por el sensor
  
  digitalWrite(LEDIV,HIGH); //Led verde indica que no hay movimiento y todo esta seguro
  digitalWrite(LEDIR,LOW); //Led Rojo indicara que hay movimiento inesperado
  
  if (value == HIGH) //Aquí indicamos que si el valor esta encendido, en el Serial mostrara que no hay obstaculo y por lo tanto en el noTOne(buzzer) no emitirá un sonido
  {
    Serial.println("No hay movimiento");
    noTone(buzzer);
  }
  //En caso contrario 
  else
  {
    digitalWrite(LEDIR,HIGH); //El Led Rojo se enciende, indicando que hay movimiento
    digitalWrite(LEDIV,LOW); //El Led Verde se apaga
    delay(1000);
    tone(buzzer,2500); //Suena un tono
    delay(1000); //Durante 150 ms
    tone(buzzer,1500); //Suena otro tono
    delay(1000); //Durante 150 ms
    noTone(buzzer);
    Serial.println("Advertencia: Hay movimiento"); //Manda un mensaje al Serial donde indica que hay movimiento
  }
  delay(100); //Se actualizara cada 100 ms  

//SISTEMA DE LUCES INTERIORES Y SISTEMA DE ABRIR-CERRAR PUERTAS POR SWITCH Y VOZ
if(BT.available()) 
{  //Si llega un dato por el puerto BT se envía al monitor Serial
  char Mensaje = BT.read(); //Guarda en la variable ?Mensaje? el dato recibido por Bluetooth
  
  /*Aqui la condicion con la app, indica que las letras Mayúculas son enviadas tanto por el control manual de la app, como con el control por voz, haciendo que se enciendan y/o 
  abra el objeto, de igual forma las Minúsculas indican que se apagan tanto por manual como por voz.*/
  
  if(Mensaje == 'A') 
  {
    Serial.println("Se encendió el Cuarto 1");
    digitalWrite(LEDR1,HIGH);
    delay(1000); 
  }
  else if(Mensaje == 'a') 
  {
    Serial.println("Se apagó el Cuarto 1");
    digitalWrite(LEDR1,LOW);
    delay(1000);
  }
  else if(Mensaje == 'B') 
  {
    Serial.println("Se encendió el Cuarto 2");
    digitalWrite(LEDR2,HIGH);
    lcd.clear();
    lcd.setCursor(3,1);
    lcd.print("SE ENCENDIO EL");
    lcd.setCursor(7,2);
    lcd.print("CUARTO 2");    
    delay(1000);
  }
  else if(Mensaje == 'b') 
  {
    Serial.println("Se apagó el Cuarto 2");
    digitalWrite(LEDR2,LOW);
    lcd.clear();
    lcd.setCursor(5,1);
    lcd.print("SE APAGO EL");
    lcd.setCursor(7,2);
    lcd.print("CUARTO 2");
    delay(1000);
  }    
  else if(Mensaje == 'C') 
  {
    Serial.println("Se encendió el Cuarto 3");
    digitalWrite(LEDR3,HIGH);
    lcd.clear();
    lcd.setCursor(3,1);
    lcd.print("SE ENCENDIO EL");
    lcd.setCursor(7,2);
    lcd.print("CUARTO 3");
    delay(1000);
  }
  else if(Mensaje == 'c') 
  {
    Serial.println("Se apagó el Cuarto 3");
    digitalWrite(LEDR3,LOW);
    lcd.clear();
    lcd.setCursor(5,1);
    lcd.print("SE APAGO EL");
    lcd.setCursor(7,2);
    lcd.print("CUARTO 3");
    delay(1000);
  }
  else if(Mensaje == 'D') 
  {
    Serial.println("Se encendió el Pasillo 1");
    digitalWrite(LEDP1,HIGH);
    lcd.clear();
    lcd.setCursor(3,1);
    lcd.print("SE ENCENDIO EL");
    lcd.setCursor(5,2);
    lcd.print("PASILLO 1");
    delay(1000);
  }
  else if(Mensaje == 'd') 
  {
    Serial.println("Se apagó el Pasillo 1");
    digitalWrite(LEDP1,LOW);
    lcd.clear();
    lcd.setCursor(5,1);
    lcd.print("SE APAGO EL");
    lcd.setCursor(5,2);
    lcd.print("PASILLO 1");
    delay(1000);
  }    
  else if(Mensaje == 'E') 
  {
    Serial.println("Se encendió el Pasillo 2");
    digitalWrite(LEDP2,HIGH);
    lcd.clear();
    lcd.setCursor(3,1);
    lcd.print("SE ENCENDIO EL");
    lcd.setCursor(5,2);
    lcd.print("PASILLO 2");
    delay(1000);
  }
  else if(Mensaje == 'e') 
  {
    Serial.println("Se apagó el Pasillo 2");
    digitalWrite(LEDP2,LOW);
    lcd.clear();
    lcd.setCursor(5,1);
    lcd.print("SE APAGO EL");
    lcd.setCursor(5,2);
    lcd.print("PASILLO 2");
    delay(1000);
  }    
  else if(Mensaje == 'F') 
  {
    Serial.println("Se encendió el Pasillo 3");
    digitalWrite(LEDP3,HIGH);
    lcd.clear();
    lcd.setCursor(3,1);
    lcd.print("SE ENCENDIO EL");
    lcd.setCursor(5,2);
    lcd.print("PASILLO 3");
    delay(1000);
  }
  else if(Mensaje == 'f') 
  {
    Serial.println("Se apagó el Pasillo 3");
    digitalWrite(LEDP3,LOW);
    lcd.clear();
    lcd.setCursor(5,1);
    lcd.print("SE APAGO EL");
    lcd.setCursor(5,2);
    lcd.print("PASILLO 3");
    delay(1000);
  }    
  else if(Mensaje == 'G') 
  {    
    Serial.println("Se encendió el Baño");
    digitalWrite(LEDBO,HIGH);
    lcd.clear();
    lcd.setCursor(3,1);
    lcd.print("SE ENCENDIO EL");
    lcd.setCursor(6,2);
    lcd.print("SANITARIO");
    delay(1000);
  }
  else if(Mensaje == 'g') 
  {
    Serial.println("Se apagó el Baño");
    digitalWrite(LEDBO,LOW);
    lcd.clear();
    lcd.setCursor(5,1);
    lcd.print("SE APAGO EL");
    lcd.setCursor(6,2);
    lcd.print("SANITARIO");
    delay(1000);
  }    
  else if(Mensaje == 'H') 
  {
    Serial.println("Se encendió la Sala");
    digitalWrite(LEDSA,HIGH);
    lcd.clear();
    lcd.setCursor(3,1);
    lcd.print("SE ENCENDIO LA");
    lcd.setCursor(8,2);
    lcd.print("SALA");
    delay(1000);
  }
  else if(Mensaje == 'h') 
  {
    Serial.println("Se apagó la Sala");
    digitalWrite(LEDSA,LOW);
    lcd.clear();
    lcd.setCursor(5,1);
    lcd.print("SE APAGO LA");
    lcd.setCursor(8,2);
    lcd.print("SALA");
    delay(1000);
  }    
  else if(Mensaje == 'I') 
  {
    Serial.println("Se encendió el Comedor");
    digitalWrite(LEDCO,HIGH);
    lcd.clear();
    lcd.setCursor(3,1);
    lcd.print("SE ENCENDIO EL");
    lcd.setCursor(7,2);
    lcd.print("COMEDOR");
    delay(1000);
  }
  else if(Mensaje == 'i') 
  {
    Serial.println("Se apagó el Comedor");
    digitalWrite(LEDCO,LOW);
    lcd.clear();
    lcd.setCursor(5,1);
    lcd.print("SE APAGO EL");
    lcd.setCursor(7,2);
    lcd.print("COMEDOR");
    delay(1000);
  }
  else if(Mensaje == 'J') 
  {
    Serial.println("Se encendió la Cocina");
    digitalWrite(LEDCA,HIGH);
    lcd.clear();
    lcd.setCursor(3,1);
    lcd.print("SE ENCENDIO LA");
    lcd.setCursor(7,2);
    lcd.print("COCINA");
    delay(1000);
  }
  else if(Mensaje == 'j') 
  {
    Serial.println("Se apagó la Cocina");
    digitalWrite(LEDCA,LOW);
    lcd.clear();
    lcd.setCursor(5,1);
    lcd.print("SE APAGO LA");
    lcd.setCursor(7,2);
    lcd.print("COCINA");
    delay(1000);
  }
  else if(Mensaje == 'K') 
  {
    Serial.println("Se encendió el Garaje");
    digitalWrite(LEDGA,HIGH);
    lcd.clear();
    lcd.setCursor(3,1);
    lcd.print("SE ENCENDIO EL");
    lcd.setCursor(7,2);
    lcd.print("GARAJE");
    delay(1000);
  }
  else if(Mensaje == 'k') 
  {
    Serial.println("Se apagó el Garaje");
    digitalWrite(LEDGA,LOW);
    lcd.clear();
    lcd.setCursor(5,1);
    lcd.print("SE APAGO EL");
    lcd.setCursor(7,2);
    lcd.print("GARAJE");
    delay(1000);
  }
  else if(Mensaje == 'L') 
  {
    Serial.println("Se encendieron los Cuartos");
    digitalWrite(LEDR1,HIGH);
    digitalWrite(LEDR2,HIGH);
    digitalWrite(LEDR3,HIGH);
    lcd.clear();
    lcd.setCursor(3,1);
    lcd.print("SE ENCENDIERON");
    lcd.setCursor(1,2);
    lcd.print("TODOS LOS CUARTOS");
    delay(1000);
  }  
  else if(Mensaje == 'l') 
  {
    Serial.println("Se apagaron los Cuartos");
    digitalWrite(LEDR1,LOW);
    digitalWrite(LEDR2,LOW);
    digitalWrite(LEDR3,LOW);
    lcd.clear();
    lcd.setCursor(4,1);
    lcd.print("SE APAGARON");
    lcd.setCursor(1,2);
    lcd.print("TODOS LOS CUARTOS");
    delay(1000);
  }
  else if(Mensaje == 'M') 
  {
    Serial.println("Se encendieron los Pasillos");
    digitalWrite(LEDP1,HIGH);
    digitalWrite(LEDP2,HIGH);
    digitalWrite(LEDP3,HIGH);
    lcd.clear();
    lcd.setCursor(3,1);
    lcd.print("SE ENCENDIERON");
    lcd.setCursor(1,2);
    lcd.print("TODOS LOS PASILLOS");
    delay(1000);
  }
  else if(Mensaje == 'm') 
  {
    Serial.println("Se apagaron los Pasillos");
    digitalWrite(LEDP1,LOW);
    digitalWrite(LEDP2,LOW);
    digitalWrite(LEDP3,LOW);
    lcd.clear();
    lcd.setCursor(4,1);
    lcd.print("SE APAGARON");
    lcd.setCursor(1,2);
    lcd.print("TODOS LOS PASILLOS");
    delay(1000);
  }
  else if(Mensaje == 'N') 
  {
    Serial.println("Se encendió toda la Casa");
    digitalWrite(LEDR1,HIGH);
    digitalWrite(LEDR2,HIGH);
    digitalWrite(LEDR3,HIGH);
    digitalWrite(LEDP1,HIGH);
    digitalWrite(LEDP2,HIGH);
    digitalWrite(LEDP3,HIGH);
    digitalWrite(LEDBO,HIGH);
    digitalWrite(LEDSA,HIGH);
    digitalWrite(LEDCO,HIGH);
    digitalWrite(LEDCA,HIGH);
    digitalWrite(LEDGA,HIGH);
    lcd.clear();
    lcd.setCursor(4,1);
    lcd.print("SE ENCENDIO");
    lcd.setCursor(4,2);
    lcd.print("TODA LA CASA");
    delay(1000);
  }
  else if(Mensaje == 'n') 
  {
    Serial.println("Se apagó toda la Casa");
    digitalWrite(LEDR1,LOW);
    digitalWrite(LEDR2,LOW);
    digitalWrite(LEDR3,LOW);
    digitalWrite(LEDP1,LOW);
    digitalWrite(LEDP2,LOW);
    digitalWrite(LEDP3,LOW);
    digitalWrite(LEDBO,LOW);
    digitalWrite(LEDSA,LOW);
    digitalWrite(LEDCO,LOW);
    digitalWrite(LEDCA,LOW);
    digitalWrite(LEDGA,LOW);
    lcd.clear();
    lcd.setCursor(6,1);
    lcd.print("SE APAGO");
    lcd.setCursor(4,2);
    lcd.print("TODA LA CASA");
    delay(1000);
  }
  
  //ABRIR O CERRAR PUERTAS POR VOZ O SWITCHES
  //Garaje 
  else if(Mensaje == 'O') 
  {
    Serial.println("Se abrio Garaje por Switch o Voz");
    digitalWrite(LEDVG,HIGH);
    digitalWrite(LEDRG,LOW);
    lcd.clear();
    lcd.setCursor(5,1);
    lcd.print("SE ABRIO EL");
    lcd.setCursor(7,2);
    lcd.print("GARAJE");
    delay(1000);    
    tone(buzzer,600);
    delay(1000);
    noTone(buzzer);
    garage.write(150);
    delay(8000);
    tone(buzzer,500);
    delay(2000);
    noTone(buzzer);
    garage.write(0);
    delay(1000);
  }
    /*No hay necesidad de poner un apartado de que se cierre la puerta manualmente, ya que el loop en la parte donde lee la distancia del ultrasónico, la puerta del garaje
  se cierra automaticamente, pero lo pondre por si en dado caso, el dato que se envia al Bluetooth no llega, con la voz se puede volver activar.*/
  else if(Mensaje == 'o') 
  {
    Serial.println("Se cerró Garaje por Switch o Voz");
    lcd.clear();
    lcd.setCursor(5,1);
    lcd.print("SE CERRO EL");
    lcd.setCursor(7,2);
    lcd.print("GARAJE");
    delay(1000);
    noTone(buzzer);
    digitalWrite(LEDVG,LOW);
    digitalWrite(LEDRG,HIGH);
    garage.write(0);   
  }
  else if(Mensaje == 'p') 
  {
    Serial.println("Se cerró la Puerta 0");
    lcd.clear();
    lcd.setCursor(5,1);
    lcd.print("SE CERRO LA");
    lcd.setCursor(7,2);
    lcd.print("PUERTA");
    puerta.write(0);
    //delay(2000);
  }
  else if(Mensaje == 'P') 
  {
    Serial.println("Se abrió la Puerta 120 grados");
    lcd.clear();
    lcd.setCursor(5,1);
    lcd.print("SE ABRIO LA");
    lcd.setCursor(7,2);
    lcd.print("PUERTA");
    delay(1000);
    puerta.write(120);
  }
  else if(Mensaje == 'Q') 
  {
    Serial.println("Se abrió la Ventana");
    lcd.clear();
    lcd.setCursor(5,1);
    lcd.print("SE ABRIO LA");
    lcd.setCursor(6,2);
    lcd.print("VENTANA");
    delay(1000);
    ventana.write(0);
    //delay(5000);
  }
  else if(Mensaje == 'q') 
  {
    Serial.println("Se cerró la Ventana");
    lcd.clear();
    lcd.setCursor(5,1);
    lcd.print("SE CERRO LA");
    lcd.setCursor(6,2);
    lcd.print("VENTANA");
    delay(1000);
    ventana.write(90);
    //delay(5000);
  }
  delay(100);
 }
}
